# Fritzing sketch LumibaerSketch (saved by Fritzing 0.9.4)

parts:
  Bauteil2 = NanoESP
  Bauteil3 = 16 NeoPixel Ring [part_number=1463]
  Bauteil4 = 16 NeoPixel Ring [part_number=1463]
  S1 = Round Pushbutton
  R1 = Resistor [tolerance=±5% resistance=220 package=THT]
  C1 = Electrolytic Capacitor [capacitance=1mF package="100 mil [THT, electrolytic]"]

nets:
  GND: Bauteil2.GND, Bauteil3.GND, Bauteil4.GND, S1.leg1, C1.-
  N1: Bauteil2.D6, R1.Pin_0
  N2: Bauteil2.D7, S1.leg0
  VDD: Bauteil2.5V, Bauteil3.VDD, Bauteil4.VDD, C1.+
  N3: Bauteil3.IN, R1.Pin_1
  N4: Bauteil3.OUT, Bauteil4.IN

notes:
  back
  front

custom parts:
  16 NeoPixel Ring: 16 ultra bright smart LED NeoPixels are arranged in a circle with 1.75" (44.5mm) outer diameter. The rings are 'chainable' - connect the output pin of one to the input pin of another. Use only one microcontroller pin to control as many as you can chain together! Each LED is addressable as the driver chip is inside the LED. Each one has ~18mA constant current drive so the color will be very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
